# Fritzing sketch pushButton Experiment (saved by Fritzing 0.9.3b)
breadboards: 1

parts:
  S1 = Pushbutton [package="[THT]"]
  R1 = Resistor [tolerance=±5% resistance=10k package="0603 [SMD]"]
  U1 = NodeMCU V1.0

nets:
  N1: S1.Pin_1, S1.Pin_2, R1.Pin_0, U1.D1
  N2: S1.Pin_3, S1.Pin_4, U1.3V3
  N3: R1.Pin_1, U1.CMD

custom parts:
  NodeMCU V1.0: ESP8266 based NodeMCU
